# Fritzing sketch 회로구성 (saved by Fritzing 0.9.3b)
breadboards: 1

parts:
  부품1 = Arduino Uno (Rev3)
  S1 = Pushbutton [package="[THT]"]  # not connected
  부품2 = HX711 Weighing Sensor Module

nets:
  GND: 부품1.GND, 부품2.GND
